# Fritzing sketch schematics (saved by Fritzing 1.0.4)
perfboards: 2

parts:
  U2 = ESP32S-HiLetgo [part_number=ESP32S-HiLetgo]
  J1 = female pin header, 2 pins [form="♀ (female)"]
  THERMISTORS = Temperature Sensor (Thermistor) [thermistor_type=NTC package=THT]
  R13 = Resistor [tolerance=±5% resistance=10k package="0402 [SMD]"]
  J8 = female pin header, 2 pins [form="♀ (female)"]
  R14 = Resistor [tolerance=±5% resistance=10k package="0402 [SMD]"]
  J9 = female pin header, 2 pins [form="♀ (female)"]
  R15 = Resistor [tolerance=±5% resistance=10k package="0402 [SMD]"]
  J10 = female pin header, 2 pins [form="♀ (female)"]
  J11 = female pin header, 2 pins [form="♀ (female)"]
  J12 = female pin header, 2 pins [form="♀ (female)"]
  R16 = Resistor [tolerance=±5% resistance=10k package="0402 [SMD]"]
  R17 = Resistor [tolerance=±5% resistance=10k package="0402 [SMD]"]
  R18 = Resistor [tolerance=±5% resistance=10k package="0402 [SMD]"]
  J13 = female pin header, 1 pin [form="♀ (female)"]
  J14 = female pin header, 1 pin [form="♀ (female)"]
  J15 = female pin header, 1 pin [form="♀ (female)"]
  J16 = female pin header, 1 pin [form="♀ (female)"]
  J17 = female pin header, 1 pin [form="♀ (female)"]
  J18 = female pin header, 1 pin [form="♀ (female)"]
  R19 = Temperature Sensor (Thermistor) [thermistor_type=NTC package=THT]
  R20 = Temperature Sensor (Thermistor) [thermistor_type=NTC package=THT]
  R21 = Temperature Sensor (Thermistor) [thermistor_type=NTC package=THT]
  R22 = Temperature Sensor (Thermistor) [thermistor_type=NTC package=THT]
  R23 = Temperature Sensor (Thermistor) [thermistor_type=NTC package=THT]
  J20 = female pin header, 4 pins [form="♀ (female)"]
  2kΩ = Resistor [tolerance=±5% resistance=2k package="0402 [SMD]"]
  R25 = Resistor [tolerance=±5% resistance=10k package="0402 [SMD]"]
  RC = Tantalum Capacitor [capacitance=0.1nF voltage=35V package="C 6032 [SMD, tantalum]"]
  12V_PWM_FAN = Fan - 4 wire [package=THT]
  5v_/_GND_/_GND_/_12V = female pin header, 4 pins [form="♀ (female)"]
  J7 = female pin header, 1 pin [form="♀ (female)"]
  J21 = female pin header, 1 pin [form="♀ (female)"]
  J22 = female pin header, 1 pin [form="♀ (female)"]
  J23 = female pin header, 1 pin [form="♀ (female)"]
  1kΩ = Resistor [tolerance=±5% resistance=1k package="0402 [SMD]"]

nets:
  N1: U2.GPIO36, J8.pin1, R14.Pin_1, J17.pin1, R19.pin_1
  N2: U2.GPIO39, J1.pin1, THERMISTORS.pin_1, R13.Pin_1, J18.pin1
  N3: U2.GPIO34, J10.pin1, R16.Pin_1, J15.pin1, R21.pin_1
  N4: U2.GPIO35, J9.pin1, R15.Pin_1, J16.pin1, R20.pin_1
  N5: U2.GPIO32, J12.pin1, R18.Pin_1, J13.pin1, R23.pin_1
  N6: U2.GPIO33, J11.pin1, R17.Pin_1, J14.pin1, R22.pin_1
  N7: U2.GND, RC.-
  N8: U2.GPIO5, J20.pin1, 12V_PWM_FAN.PWM
  N9: U2.GPIO22, RC.+, 1kΩ.Pin_0
  N10: J1.pin2, THERMISTORS.pin_0, J8.pin2, J9.pin2, J10.pin2, J11.pin2, J12.pin2, R19.pin_0, R20.pin_0, R21.pin_0, R22.pin_0, R23.pin_0
  N11: R18.Pin_0, 5v_/_GND_/_GND_/_12V.pin1, J22.pin1, J23.pin1
  N12: J20.pin2, 2kΩ.Pin_0, R25.Pin_1, 12V_PWM_FAN.Tach
  N13: J20.pin3, 12V_PWM_FAN.Power
  N14: J20.pin4, 12V_PWM_FAN.GND, 5v_/_GND_/_GND_/_12V.pin3, J7.pin1, J21.pin1
  N15: 2kΩ.Pin_1, 1kΩ.Pin_1

custom parts:
  ESP32S-HiLetgo: HiLetgo ESP-WROOM-32 ESP32 ESP-32S Development Board 2.4GHz Dual-Mode WiFi + Bluetooth Dual Cores Microcontroller The ESP32 integrated with Antenna switches, RF Balun, power amplifiers, low-noise amplifiers, filters, and management modules, and the entire solution occupies the least area of PCB. 2.4 GHz Wi-Fi plus Bluetooth dual-mode chip, with TSMC Ultra-low power consumption 40nm technology,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
  Fan - 4 wire: Fan, 4 wire with tach.
